# Fritzing sketch wiring-diagram (saved by Fritzing 0.9.4)
breadboards: 1

parts:
  MCU1 = Raspberry Pi Zero
  LCD1 = LCD screen
  S2 = Pushbutton [package="[SMD]"]
  R1 = Resistor [tolerance=±5% resistance=1k package=THT]
  U3 = POT [package=trim_pot]

nets:
  N1: MCU1.pin_2, MCU1.pin_4, LCD1.VDD
  N2: MCU1.pin_5, S2.Pin_3, S2.Pin_4, R1.Pin_0
  N3: MCU1.pin_6, MCU1.pin_34, MCU1.pin_39, LCD1.VSS, LCD1.R/W, LCD1.LED-, S2.Pin_1, S2.Pin_2, R1.Pin_1, U3.S
  N4: MCU1.pin_21, LCD1.LED+
  N5: MCU1.pin_23, LCD1.DB7
  N6: MCU1.pin_29, LCD1.DB6
  N7: MCU1.pin_31, LCD1.DB5
  N8: MCU1.pin_33, LCD1.DB4
  N9: MCU1.pin_35, LCD1.E
  N10: MCU1.pin_37, LCD1.RS
  N11: LCD1.V0, U3.E
